# Fritzing sketch hookup-uno-photon (saved by Fritzing 0.9.3b)
breadboards: 1

parts:
  Part1 = Arduino Uno (Rev3)
  Part2 = Photon
  LED1 = LED - 5mm [color="Red (633nm)" package="5 mm [THT]"]
  R1 = Resistor [tolerance=±5% resistance=220 package=THT]

nets:
  N1: Part1.D9_PWM, LED1.anode
  N2: Part1.A4/SDA, Part2.D0
  N3: Part1.A5/SCL, Part2.D1
  N4: Part1.GND, R1.Pin_0
  N5: LED1.cathode, R1.Pin_1

notes:
  <- (i2c) SCL
  <- (i2c) SDA
